// Logisim project CPU MIPS.circ as structural Verilog: 7 circuits, main circuit main
module main (
  input  Write_Enable,
  input  reset
);

  wire alu_control_1_invert, and_1_out, clock_1_out, control_unit_1_alusrc, control_unit_1_beq,
       control_unit_1_memread, control_unit_1_memtoreg, control_unit_1_memwr, control_unit_1_regdst,
       control_unit_1_regwr, ual_8_bit_1_zf;
  wire [1:0] alu_control_1_alu_code;
  wire [2:0] multiplexer_1_out, ram_1_data_3;
  wire [6:0] ram_1_data;
  wire [7:0] adder_1_out, adder_2_out, banc_de_registre_1_a, banc_de_registre_1_b, bit_extender_1_out,
       control_unit_1_alu_control, multiplexer_2_out, multiplexer_3_out, multiplexer_4_out, ram_2_data,
       registre_1_out_12, shifter_1_out, ual_8_bit_1_res;
  wire [12:7] ram_1_data_2;

  Clock clock_1 (.out(clock_1_out));
  Registre registre_1 (
    .out_12(registre_1_out_12[0]), .out_13(registre_1_out_12[1]), .out_14(registre_1_out_12[2]),
    .out_15(registre_1_out_12[3]), .out_16(registre_1_out_12[4]), .out_17(registre_1_out_12[5]),
    .out_18(registre_1_out_12[6]), .out_19(registre_1_out_12[7]), .Write_Enable(Write_Enable),
    .in_2(multiplexer_3_out[0]), .in_3(multiplexer_3_out[1]), .in_4(multiplexer_3_out[2]),
    .in_5(multiplexer_3_out[3]), .in_6(multiplexer_3_out[4]), .in_7(multiplexer_3_out[5]),
    .in_8(multiplexer_3_out[6]), .in_9(multiplexer_3_out[7]), .Clk(clock_1_out), .reset(reset));
  Adder adder_1 (.a(registre_1_out_12), .b(8'h1), .out(adder_1_out));  // open: cin, cout
  RAM #(.dataWidth(16)) ram_1 (
    .addr(registre_1_out_12), .data({ram_1_data_3, ram_1_data_2, ram_1_data}), .clk(clock_1_out));  // open: sel, ld, clr
  assign bit_extender_1_out = {{1{ram_1_data[6]}}, ram_1_data};  // Bit_Extender bit_extender_1
  Control_Unit control_unit_1 (
    .OpCode(ram_1_data_3), .RegDst(control_unit_1_regdst), .ALUSrc(control_unit_1_alusrc),
    .MemToReg(control_unit_1_memtoreg), .RegWr(control_unit_1_regwr), .MemWr(control_unit_1_memwr),
    .Beq(control_unit_1_beq), .MemRead(control_unit_1_memread), .ALU_Control(control_unit_1_alu_control));
  Multiplexer #(.width(3), .enable("false")) multiplexer_1 (
    .in0(ram_1_data_2[9:7]), .in1(ram_1_data[6:4]), .out(multiplexer_1_out), .sel(control_unit_1_regdst));
  Banc_de_Registre banc_de_registre_1 (
    .Write_Enable(control_unit_1_regwr), .Clk(clock_1_out), .A(banc_de_registre_1_a),
    .B(banc_de_registre_1_b), .Data_in(multiplexer_4_out), .RW(multiplexer_1_out), .RA(ram_1_data_2[12:10]),
    .RB(ram_1_data_2[9:7]));
  Multiplexer #(.width(8), .enable("false")) multiplexer_2 (
    .in0(banc_de_registre_1_b), .in1(bit_extender_1_out), .out(multiplexer_2_out), .sel(control_unit_1_alusrc));
  Adder adder_2 (.a(adder_1_out), .b(shifter_1_out), .out(adder_2_out));  // open: cin, cout
  Shifter shifter_1 (.in(bit_extender_1_out), .\dist (3'b010), .out(shifter_1_out));
  and and_1 (and_1_out, control_unit_1_beq, ual_8_bit_1_zf);
  UAL_8_bit ual_8_bit_1 (
    .invert(alu_control_1_invert), .res(ual_8_bit_1_res), .ZF(ual_8_bit_1_zf), .B(multiplexer_2_out),
    .A(banc_de_registre_1_a), .Select(alu_control_1_alu_code));  // open: OF, CF
  ALU_Control alu_control_1 (
    .CU_input(control_unit_1_alu_control), .inst_2_0(ram_1_data[2:0]), .ALU_Code(alu_control_1_alu_code),
    .invert(alu_control_1_invert));
  Multiplexer #(.width(8), .enable("false")) multiplexer_3 (
    .in0(adder_1_out), .in1(adder_2_out), .out(multiplexer_3_out), .sel(and_1_out));
  RAM #(.bus("separate")) ram_2 (
    .addr(ual_8_bit_1_res), .din(banc_de_registre_1_b), .data(ram_2_data), .str(control_unit_1_memwr),
    .clk(clock_1_out), .ld(control_unit_1_memread));  // open: sel, clr
  Multiplexer #(.width(8), .enable("false")) multiplexer_4 (
    .in0(ual_8_bit_1_res), .in1(ram_2_data), .out(multiplexer_4_out), .sel(control_unit_1_memtoreg));

  // Notes on the sheet:
  //   RegWr
  //   Inst[0-6]
  //   Branch
  //   Mem Read
  //   MemToReg
  //   MemWr
  //   ALUSrc
  //   RegDst
  //   Shift
  //   Left 2
  //   ALUSrc
  //   Equal
  //   invert
  //   Select
  //   nPCsel
  //   MemWr
  //   Mem Read
  //   MemToReg
endmodule

module UAL_1_bit (
  input  invert,
  input  [1:0] Select,
  input  Cin,
  input  A,
  input  e3,
  input  B,
  output Res,
  output S,
  output Cout
);

  wire and_1_out, and_2_out, and_3_out, multiplexer_1_out, not_1_out, or_1_out, xor_1_out;

  not not_1 (not_1_out, B);
  Multiplexer #(.enable("false")) multiplexer_1 (.in0(B), .in1(not_1_out), .out(multiplexer_1_out), .sel(invert));
  and and_1 (and_1_out, multiplexer_1_out, A);
  and and_2 (and_2_out, A, multiplexer_1_out);
  or or_1 (or_1_out, multiplexer_1_out, A);
  xor xor_1 (xor_1_out, A, multiplexer_1_out);
  and and_3 (and_3_out, xor_1_out, Cin);
  xor xor_2 (Cout, and_1_out, and_3_out);
  xor xor_3 (S, Cin, xor_1_out);
  Multiplexer #(.select(2), .enable("false")) multiplexer_2 (
    .in0(and_2_out), .in1(or_1_out), .in2(S), .in3(e3), .out(Res), .sel(Select));

  // Notes on the sheet:
  //   AND
  //   OR
  //   S
endmodule

// ALU 8-bit
module UAL_8_bit (
  input  [7:0] A,
  input  [1:0] Select,
  input  invert,
  input  [7:0] B,
  output [7:0] res,
  output ZF,
  output CF,
  output OF
);

  wire ual_1_bit_1_cout, ual_1_bit_2_cout, ual_1_bit_3_cout, ual_1_bit_4_cout, ual_1_bit_5_cout,
       ual_1_bit_6_cout, ual_1_bit_7_cout, ual_1_bit_8_s;

  UAL_1_bit ual_1_bit_1 (
    .Select(Select), .A(A[0]), .B(B[0]), .Res(res[0]), .invert(invert), .Cin(invert),
    .Cout(ual_1_bit_1_cout), .e3(ual_1_bit_8_s));  // open: S
  UAL_1_bit ual_1_bit_2 (
    .Select(Select), .A(A[1]), .B(B[1]), .Res(res[1]), .invert(invert), .Cin(ual_1_bit_1_cout),
    .Cout(ual_1_bit_2_cout), .e3(1'b0));  // open: S
  UAL_1_bit ual_1_bit_3 (
    .Select(Select), .A(A[2]), .B(B[2]), .Res(res[2]), .invert(invert), .Cin(ual_1_bit_2_cout),
    .Cout(ual_1_bit_3_cout), .e3(1'b0));  // open: S
  UAL_1_bit ual_1_bit_4 (
    .Select(Select), .A(A[3]), .B(B[3]), .Res(res[3]), .invert(invert), .Cin(ual_1_bit_3_cout),
    .Cout(ual_1_bit_4_cout), .e3(1'b0));  // open: S
  UAL_1_bit ual_1_bit_5 (
    .Select(Select), .A(A[4]), .B(B[4]), .Res(res[4]), .invert(invert), .Cin(ual_1_bit_4_cout),
    .Cout(ual_1_bit_5_cout), .e3(1'b0));  // open: S
  UAL_1_bit ual_1_bit_6 (
    .Select(Select), .A(A[5]), .B(B[5]), .Res(res[5]), .invert(invert), .Cin(ual_1_bit_5_cout),
    .Cout(ual_1_bit_6_cout), .e3(1'b0));  // open: S
  UAL_1_bit ual_1_bit_7 (
    .Select(Select), .A(A[6]), .B(B[6]), .Res(res[6]), .invert(invert), .Cin(ual_1_bit_6_cout),
    .Cout(ual_1_bit_7_cout), .e3(1'b0));  // open: S
  UAL_1_bit ual_1_bit_8 (
    .Select(Select), .A(A[7]), .B(B[7]), .Res(res[7]), .invert(invert), .Cin(ual_1_bit_7_cout), .Cout(CF),
    .e3(1'b0), .S(ual_1_bit_8_s));
  xor xor_1 (OF, CF, ual_1_bit_7_cout);
  nor nor_1 (ZF, res[0], res[1], res[2], res[3], res[4], res[5], res[6], res[7]);
endmodule

module Registre (
  input  Write_Enable,
  input  in_2,
  input  in_3,
  input  in_4,
  input  in_5,
  input  in_6,
  input  in_7,
  input  in_8,
  input  in_9,
  input  Clk,
  input  reset,
  output out_12,
  output out_13,
  output out_14,
  output out_15,
  output out_16,
  output out_17,
  output out_18,
  output out_19
);

  D_Flip_Flop d_ff_1 (.clk(Clk), .D(in_2), .Q(out_12), .en(Write_Enable), .reset(reset));  // open: Qn, preset
  D_Flip_Flop d_ff_2 (.clk(Clk), .D(in_3), .Q(out_13), .en(Write_Enable), .reset(reset));  // open: Qn, preset
  D_Flip_Flop d_ff_3 (.clk(Clk), .D(in_4), .Q(out_14), .en(Write_Enable), .reset(reset));  // open: Qn, preset
  D_Flip_Flop d_ff_4 (.clk(Clk), .D(in_5), .Q(out_15), .en(Write_Enable), .reset(reset));  // open: Qn, preset
  D_Flip_Flop d_ff_5 (.clk(Clk), .D(in_6), .Q(out_16), .en(Write_Enable), .reset(reset));  // open: Qn, preset
  D_Flip_Flop d_ff_6 (.clk(Clk), .D(in_7), .Q(out_17), .en(Write_Enable), .reset(reset));  // open: Qn, preset
  D_Flip_Flop d_ff_7 (.clk(Clk), .D(in_8), .Q(out_18), .en(Write_Enable), .reset(reset));  // open: Qn, preset
  D_Flip_Flop d_ff_8 (.clk(Clk), .D(in_9), .Q(out_19), .en(Write_Enable), .reset(reset));  // open: Qn, preset
endmodule

// 8 8-bit Registers
module Banc_de_Registre (
  input  [2:0] RW,
  input  [2:0] RA,
  input  [2:0] RB,
  input  Write_Enable,
  input  [7:0] Data_in,
  input  Clk,
  output [7:0] A,
  output [7:0] B
);

  wire demultiplexer_1_out0, demultiplexer_1_out1, demultiplexer_1_out2, demultiplexer_1_out3,
       demultiplexer_1_out4, demultiplexer_1_out5, demultiplexer_1_out6, demultiplexer_1_out7;
  wire [7:0] registre_1_out_12, registre_2_out_12, registre_3_out_12, registre_4_out_12, registre_5_out_12,
       registre_6_out_12, registre_7_out_12, registre_8_out_12;

  Demultiplexer #(.select(3), .enable("false")) demultiplexer_1 (
    .out0(demultiplexer_1_out0), .out1(demultiplexer_1_out1), .out2(demultiplexer_1_out2),
    .out3(demultiplexer_1_out3), .out4(demultiplexer_1_out4), .out5(demultiplexer_1_out5),
    .out6(demultiplexer_1_out6), .out7(demultiplexer_1_out7), .in(Write_Enable), .sel(RW));
  Registre registre_1 (
    .out_12(registre_1_out_12[0]), .out_13(registre_1_out_12[1]), .out_14(registre_1_out_12[2]),
    .out_15(registre_1_out_12[3]), .out_16(registre_1_out_12[4]), .out_17(registre_1_out_12[5]),
    .out_18(registre_1_out_12[6]), .out_19(registre_1_out_12[7]), .Write_Enable(demultiplexer_1_out0),
    .in_2(1'b0), .in_3(1'b0), .in_4(1'b0), .in_5(1'b0), .in_6(1'b0), .in_7(1'b0), .in_8(1'b0), .in_9(1'b0),
    .Clk(Clk), .reset(demultiplexer_1_out1));
  Registre registre_2 (
    .out_12(registre_2_out_12[0]), .out_13(registre_2_out_12[1]), .out_14(registre_2_out_12[2]),
    .out_15(registre_2_out_12[3]), .out_16(registre_2_out_12[4]), .out_17(registre_2_out_12[5]),
    .out_18(registre_2_out_12[6]), .out_19(registre_2_out_12[7]), .Write_Enable(demultiplexer_1_out1),
    .in_2(Data_in[0]), .in_3(Data_in[1]), .in_4(Data_in[2]), .in_5(Data_in[3]), .in_6(Data_in[4]),
    .in_7(Data_in[5]), .in_8(Data_in[6]), .in_9(Data_in[7]), .Clk(Clk));  // open: reset
  Registre registre_3 (
    .out_12(registre_3_out_12[0]), .out_13(registre_3_out_12[1]), .out_14(registre_3_out_12[2]),
    .out_15(registre_3_out_12[3]), .out_16(registre_3_out_12[4]), .out_17(registre_3_out_12[5]),
    .out_18(registre_3_out_12[6]), .out_19(registre_3_out_12[7]), .Write_Enable(demultiplexer_1_out2),
    .in_2(Data_in[0]), .in_3(Data_in[1]), .in_4(Data_in[2]), .in_5(Data_in[3]), .in_6(Data_in[4]),
    .in_7(Data_in[5]), .in_8(Data_in[6]), .in_9(Data_in[7]), .Clk(Clk));  // open: reset
  Registre registre_4 (
    .out_12(registre_4_out_12[0]), .out_13(registre_4_out_12[1]), .out_14(registre_4_out_12[2]),
    .out_15(registre_4_out_12[3]), .out_16(registre_4_out_12[4]), .out_17(registre_4_out_12[5]),
    .out_18(registre_4_out_12[6]), .out_19(registre_4_out_12[7]), .Write_Enable(demultiplexer_1_out3),
    .in_2(Data_in[0]), .in_3(Data_in[1]), .in_4(Data_in[2]), .in_5(Data_in[3]), .in_6(Data_in[4]),
    .in_7(Data_in[5]), .in_8(Data_in[6]), .in_9(Data_in[7]), .Clk(Clk));  // open: reset
  Registre registre_5 (
    .out_12(registre_5_out_12[0]), .out_13(registre_5_out_12[1]), .out_14(registre_5_out_12[2]),
    .out_15(registre_5_out_12[3]), .out_16(registre_5_out_12[4]), .out_17(registre_5_out_12[5]),
    .out_18(registre_5_out_12[6]), .out_19(registre_5_out_12[7]), .Write_Enable(demultiplexer_1_out4),
    .in_2(Data_in[0]), .in_3(Data_in[1]), .in_4(Data_in[2]), .in_5(Data_in[3]), .in_6(Data_in[4]),
    .in_7(Data_in[5]), .in_8(Data_in[6]), .in_9(Data_in[7]), .Clk(Clk));  // open: reset
  Registre registre_6 (
    .out_12(registre_6_out_12[0]), .out_13(registre_6_out_12[1]), .out_14(registre_6_out_12[2]),
    .out_15(registre_6_out_12[3]), .out_16(registre_6_out_12[4]), .out_17(registre_6_out_12[5]),
    .out_18(registre_6_out_12[6]), .out_19(registre_6_out_12[7]), .Write_Enable(demultiplexer_1_out5),
    .in_2(Data_in[0]), .in_3(Data_in[1]), .in_4(Data_in[2]), .in_5(Data_in[3]), .in_6(Data_in[4]),
    .in_7(Data_in[5]), .in_8(Data_in[6]), .in_9(Data_in[7]), .Clk(Clk));  // open: reset
  Registre registre_7 (
    .out_12(registre_7_out_12[0]), .out_13(registre_7_out_12[1]), .out_14(registre_7_out_12[2]),
    .out_15(registre_7_out_12[3]), .out_16(registre_7_out_12[4]), .out_17(registre_7_out_12[5]),
    .out_18(registre_7_out_12[6]), .out_19(registre_7_out_12[7]), .Write_Enable(demultiplexer_1_out6),
    .in_2(Data_in[0]), .in_3(Data_in[1]), .in_4(Data_in[2]), .in_5(Data_in[3]), .in_6(Data_in[4]),
    .in_7(Data_in[5]), .in_8(Data_in[6]), .in_9(Data_in[7]), .Clk(Clk));  // open: reset
  Registre registre_8 (
    .out_12(registre_8_out_12[0]), .out_13(registre_8_out_12[1]), .out_14(registre_8_out_12[2]),
    .out_15(registre_8_out_12[3]), .out_16(registre_8_out_12[4]), .out_17(registre_8_out_12[5]),
    .out_18(registre_8_out_12[6]), .out_19(registre_8_out_12[7]), .Write_Enable(demultiplexer_1_out7),
    .in_2(Data_in[0]), .in_3(Data_in[1]), .in_4(Data_in[2]), .in_5(Data_in[3]), .in_6(Data_in[4]),
    .in_7(Data_in[5]), .in_8(Data_in[6]), .in_9(Data_in[7]), .Clk(Clk));  // open: reset
  Multiplexer #(.select(3), .width(8), .enable("false")) multiplexer_1 (
    .in0(registre_1_out_12), .in1(registre_2_out_12), .in2(registre_3_out_12), .in3(registre_4_out_12),
    .in4(registre_5_out_12), .in5(registre_6_out_12), .in6(registre_7_out_12), .in7(registre_8_out_12),
    .out(A), .sel(RA));
  Multiplexer #(.select(3), .width(8), .enable("false")) multiplexer_2 (
    .in0(registre_1_out_12), .in1(registre_2_out_12), .in2(registre_3_out_12), .in3(registre_4_out_12),
    .in4(registre_5_out_12), .in5(registre_6_out_12), .in6(registre_7_out_12), .in7(registre_8_out_12),
    .out(B), .sel(RB));

  // Notes on the sheet:
  //   zero
  //   at
  //   Data in
  //   v0
  //   v1
  //   a0
  //   a1
  //   a2
  //   a3
  //   A
  //   B
endmodule

module Control_Unit (
  input  [2:0] OpCode,
  output RegDst,
  output ALUSrc,
  output MemToReg,
  output RegWr,
  output MemWr,
  output Beq,
  output MemRead,
  output [7:0] ALU_Control
);

  nor R_Type (ALU_Control[7], OpCode[0], OpCode[1], OpCode[2]);
  and SUBi (ALU_Control[5], OpCode[2], ~OpCode[1], OpCode[0]);  // AND_Gate
  and ADDi (ALU_Control[6], OpCode[2], ~OpCode[1], ~OpCode[0]);  // AND_Gate
  and ORi (ALU_Control[3], OpCode[2], OpCode[1], ~OpCode[0]);  // AND_Gate
  and ANDi (ALU_Control[4], OpCode[2], OpCode[1], OpCode[0]);
  and u_Beq (ALU_Control[2], ~OpCode[2], ~OpCode[1], OpCode[0]);  // AND_Gate
  and lw (ALU_Control[1], ~OpCode[0], OpCode[1], ~OpCode[2]);  // AND_Gate
  and sw (ALU_Control[0], ~OpCode[2], OpCode[1], OpCode[0]);  // AND_Gate
  or or_1 (ALUSrc, ALU_Control[6], ALU_Control[5], ALU_Control[4], ALU_Control[2], ALU_Control[3], ALU_Control[1], ALU_Control[0]);
  or or_2 (RegWr, ALU_Control[1], ALU_Control[7], ALU_Control[6], ALU_Control[5], ALU_Control[4], ALU_Control[3]);

  assign Beq = ALU_Control[2];
  assign MemRead = ALU_Control[1];
  assign MemToReg = ALU_Control[1];
  assign MemWr = ALU_Control[0];
  assign RegDst = ALU_Control[7];
endmodule

module ALU_Control (
  input  [7:0] CU_input,
  input  [2:0] inst_2_0,
  output [1:0] ALU_Code,
  output invert
);

  wire and_2_out, and_3_out, AND_out, or_2_out, or_3_out, or_4_out, OR_out, priority_encoder_1_en_out,
       slt_out;

  and slt (slt_out, inst_2_0[2], ~inst_2_0[1], inst_2_0[0], CU_input[7]);  // AND_Gate
  and AND (AND_out, CU_input[7], inst_2_0[0], inst_2_0[1], ~inst_2_0[2]);  // AND_Gate
  and OR (OR_out, ~inst_2_0[0], inst_2_0[1], ~inst_2_0[2], CU_input[7]);  // AND_Gate
  and and_2 (and_2_out, CU_input[7], ~inst_2_0[1], ~inst_2_0[2]);  // AND_Gate
  or or_2 (or_2_out, AND_out, CU_input[4]);
  or or_3 (or_3_out, CU_input[3], OR_out);
  or or_4 (or_4_out, CU_input[0], CU_input[1], CU_input[2], CU_input[5], CU_input[6], and_2_out);
  and and_3 (and_3_out, inst_2_0[0], ~inst_2_0[1], CU_input[7]);  // AND_Gate
  or or_5 (invert, CU_input[2], CU_input[5], and_3_out);
  Priority_Encoder #(.select(2)) priority_encoder_1 (
    .in0(or_2_out), .in1(or_3_out), .in2(or_4_out), .in3(slt_out), .out(ALU_Code),
    .en_out(priority_encoder_1_en_out), .en_in(1'b1));  // open: gs
  // also tied to VCC on the sheet: priority_encoder_1_en_out

  // Notes on the sheet:
  //   add UAL
endmodule
